// Logisim project project_1.circ as structural Verilog: 5 circuits, main circuit Part-2c
module Part_2c (
  input  [7:0] Load,
  input  L_H,
  input  [15:0] Clear,
  input  [1:0] FunSel,
  input  Clock,
  input  E,
  output [15:0] Q
);

  wire adder_1_cout, adder_2_cout, adder_3_cout, adder_4_cout, adder_5_cout, adder_6_cout, adder_7_cout,
       adder_8_cout, adder_9_cout, adder_10_cout, adder_11_cout, adder_12_cout, adder_13_cout, adder_14_cout,
       adder_15_cout, adder_17_cout, adder_18_cout, adder_19_cout, adder_20_cout, adder_21_cout,
       adder_22_cout, adder_23_cout, adder_25_cout, adder_26_cout, adder_27_cout, adder_28_cout,
       adder_29_cout, adder_30_cout, adder_31_cout;
  wire [15:0] adder_1_out, adder_17_out, multiplexer_1_out, multiplexer_2_out;

  Adder #(.width(1)) adder_1 (.a(Q[0]), .b(FunSel[1]), .out(adder_1_out[0]), .cout(adder_1_cout));  // open: cin
  Adder #(.width(1)) adder_2 (.a(Q[1]), .b(FunSel[1]), .out(adder_1_out[1]), .cin(adder_1_cout), .cout(adder_2_cout));
  Adder #(.width(1)) adder_3 (.a(Q[2]), .b(FunSel[1]), .out(adder_1_out[2]), .cin(adder_2_cout), .cout(adder_3_cout));
  Adder #(.width(1)) adder_4 (.a(Q[3]), .b(FunSel[1]), .out(adder_1_out[3]), .cin(adder_3_cout), .cout(adder_4_cout));
  Adder #(.width(1)) adder_5 (.a(Q[4]), .b(FunSel[1]), .out(adder_1_out[4]), .cin(adder_4_cout), .cout(adder_5_cout));
  Adder #(.width(1)) adder_6 (.a(Q[5]), .b(FunSel[1]), .out(adder_1_out[5]), .cin(adder_5_cout), .cout(adder_6_cout));
  Adder #(.width(1)) adder_7 (.a(Q[6]), .b(FunSel[1]), .out(adder_1_out[6]), .cin(adder_6_cout), .cout(adder_7_cout));
  Adder #(.width(1)) adder_8 (.a(Q[7]), .b(FunSel[1]), .out(adder_1_out[7]), .cin(adder_7_cout), .cout(adder_8_cout));
  Adder #(.width(1)) adder_9 (.a(Q[8]), .b(FunSel[1]), .out(adder_1_out[8]), .cin(adder_8_cout), .cout(adder_9_cout));
  Adder #(.width(1)) adder_10 (.a(Q[9]), .b(FunSel[1]), .out(adder_1_out[9]), .cin(adder_9_cout), .cout(adder_10_cout));
  Adder #(.width(1)) adder_11 (
    .a(Q[10]), .b(FunSel[1]), .out(adder_1_out[10]), .cin(adder_10_cout), .cout(adder_11_cout));
  Adder #(.width(1)) adder_12 (
    .a(Q[11]), .b(FunSel[1]), .out(adder_1_out[11]), .cin(adder_11_cout), .cout(adder_12_cout));
  Adder #(.width(1)) adder_13 (
    .a(Q[12]), .b(FunSel[1]), .out(adder_1_out[12]), .cin(adder_12_cout), .cout(adder_13_cout));
  Adder #(.width(1)) adder_14 (
    .a(Q[13]), .b(FunSel[1]), .out(adder_1_out[13]), .cin(adder_13_cout), .cout(adder_14_cout));
  Adder #(.width(1)) adder_15 (
    .a(Q[14]), .b(FunSel[1]), .out(adder_1_out[14]), .cin(adder_14_cout), .cout(adder_15_cout));
  Adder #(.width(1)) adder_16 (.a(Q[15]), .b(FunSel[1]), .out(adder_1_out[15]), .cin(adder_15_cout));  // open: cout
  Adder #(.width(1)) adder_17 (.a(Q[0]), .b(FunSel[0]), .out(adder_17_out[0]), .cout(adder_17_cout));  // open: cin
  Adder #(.width(1)) adder_18 (
    .a(Q[1]), .b(FunSel[1]), .out(adder_17_out[1]), .cin(adder_17_cout), .cout(adder_18_cout));
  Adder #(.width(1)) adder_19 (
    .a(Q[2]), .b(FunSel[1]), .out(adder_17_out[2]), .cin(adder_18_cout), .cout(adder_19_cout));
  Adder #(.width(1)) adder_20 (
    .a(Q[3]), .b(FunSel[1]), .out(adder_17_out[3]), .cin(adder_19_cout), .cout(adder_20_cout));
  Adder #(.width(1)) adder_21 (
    .a(Q[4]), .b(FunSel[1]), .out(adder_17_out[4]), .cin(adder_20_cout), .cout(adder_21_cout));
  Adder #(.width(1)) adder_22 (
    .a(Q[5]), .b(FunSel[1]), .out(adder_17_out[5]), .cin(adder_21_cout), .cout(adder_22_cout));
  Adder #(.width(1)) adder_23 (
    .a(Q[6]), .b(FunSel[1]), .out(adder_17_out[6]), .cin(adder_22_cout), .cout(adder_23_cout));
  Adder #(.width(1)) adder_24 (.a(Q[7]), .b(FunSel[1]), .out(adder_17_out[7]), .cin(adder_23_cout));  // open: cout
  Adder #(.width(1)) adder_25 (.a(Q[8]), .b(FunSel[1]), .out(adder_17_out[8]), .cout(adder_25_cout));  // open: cin
  Adder #(.width(1)) adder_26 (
    .a(Q[9]), .b(FunSel[1]), .out(adder_17_out[9]), .cin(adder_25_cout), .cout(adder_26_cout));
  Adder #(.width(1)) adder_27 (
    .a(Q[10]), .b(FunSel[1]), .out(adder_17_out[10]), .cin(adder_26_cout), .cout(adder_27_cout));
  Adder #(.width(1)) adder_28 (
    .a(Q[11]), .b(FunSel[1]), .out(adder_17_out[11]), .cin(adder_27_cout), .cout(adder_28_cout));
  Adder #(.width(1)) adder_29 (
    .a(Q[12]), .b(FunSel[1]), .out(adder_17_out[12]), .cin(adder_28_cout), .cout(adder_29_cout));
  Adder #(.width(1)) adder_30 (
    .a(Q[13]), .b(FunSel[1]), .out(adder_17_out[13]), .cin(adder_29_cout), .cout(adder_30_cout));
  Adder #(.width(1)) adder_31 (
    .a(Q[14]), .b(FunSel[1]), .out(adder_17_out[14]), .cin(adder_30_cout), .cout(adder_31_cout));
  Adder #(.width(1)) adder_32 (.a(Q[15]), .b(FunSel[1]), .out(adder_17_out[15]), .cin(adder_31_cout));  // open: cout
  Multiplexer #(.width(16), .enable("false")) multiplexer_1 (
    .in0({Load, Q[7:0]}), .in1({Q[15:8], Load}), .out(multiplexer_1_out), .sel(L_H));
  Multiplexer #(.select(2), .width(16)) multiplexer_2 (
    .in0(Clear), .in1(adder_17_out), .in2(adder_1_out), .in3(multiplexer_1_out), .out(multiplexer_2_out),
    .sel(FunSel), .en(E));
  Clock clock_1 ();  // open: out
  D_Flip_Flop d_ff_1 (.clk(Clock), .D(multiplexer_2_out[0]), .Q(Q[0]));  // open: Qn, preset, en, reset
  D_Flip_Flop d_ff_2 (.clk(Clock), .D(multiplexer_2_out[1]), .Q(Q[1]));  // open: Qn, preset, en, reset
  D_Flip_Flop d_ff_3 (.clk(Clock), .D(multiplexer_2_out[2]), .Q(Q[2]));  // open: Qn, preset, en, reset
  D_Flip_Flop d_ff_4 (.clk(Clock), .D(multiplexer_2_out[3]), .Q(Q[3]));  // open: Qn, preset, en, reset
  D_Flip_Flop d_ff_5 (.clk(Clock), .D(multiplexer_2_out[4]), .Q(Q[4]));  // open: Qn, preset, en, reset
  D_Flip_Flop d_ff_6 (.clk(Clock), .D(multiplexer_2_out[5]), .Q(Q[5]));  // open: Qn, preset, en, reset
  D_Flip_Flop d_ff_7 (.clk(Clock), .D(multiplexer_2_out[6]), .Q(Q[6]));  // open: Qn, preset, en, reset
  D_Flip_Flop d_ff_8 (.clk(Clock), .D(multiplexer_2_out[7]), .Q(Q[7]));  // open: Qn, preset, en, reset
  D_Flip_Flop d_ff_9 (.clk(Clock), .D(multiplexer_2_out[8]), .Q(Q[8]));  // open: Qn, preset, en, reset
  D_Flip_Flop d_ff_10 (.clk(Clock), .D(multiplexer_2_out[9]), .Q(Q[9]));  // open: Qn, preset, en, reset
  D_Flip_Flop d_ff_11 (.clk(Clock), .D(multiplexer_2_out[10]), .Q(Q[10]));  // open: Qn, preset, en, reset
  D_Flip_Flop d_ff_12 (.clk(Clock), .D(multiplexer_2_out[11]), .Q(Q[11]));  // open: Qn, preset, en, reset
  D_Flip_Flop d_ff_13 (.clk(Clock), .D(multiplexer_2_out[12]), .Q(Q[12]));  // open: Qn, preset, en, reset
  D_Flip_Flop d_ff_14 (.clk(Clock), .D(multiplexer_2_out[13]), .Q(Q[13]));  // open: Qn, preset, en, reset
  D_Flip_Flop d_ff_15 (.clk(Clock), .D(multiplexer_2_out[14]), .Q(Q[14]));  // open: Qn, preset, en, reset
  D_Flip_Flop d_ff_16 (.clk(Clock), .D(multiplexer_2_out[15]), .Q(Q[15]));  // open: Qn, preset, en, reset
endmodule

module _8_bit_Register (
  input  [7:0] Clear,
  input  [7:0] Load,
  input  Clock,
  input  [1:0] FunSel,
  input  E,
  output [7:0] Q
);

  wire adder_1_cout, adder_2_cout, adder_3_cout, adder_4_cout, adder_5_cout, adder_6_cout, adder_7_cout,
       adder_9_cout, adder_10_cout, adder_11_cout, adder_12_cout, adder_13_cout, adder_14_cout, adder_15_cout;
  wire [7:0] adder_1_out, adder_9_out, multiplexer_1_out;

  Adder #(.width(1)) adder_1 (.a(Q[0]), .b(FunSel[1]), .out(adder_1_out[0]), .cout(adder_1_cout));  // open: cin
  Adder #(.width(1)) adder_2 (.a(Q[1]), .b(FunSel[1]), .out(adder_1_out[1]), .cin(adder_1_cout), .cout(adder_2_cout));
  Adder #(.width(1)) adder_3 (.a(Q[2]), .b(FunSel[1]), .out(adder_1_out[2]), .cin(adder_2_cout), .cout(adder_3_cout));
  Adder #(.width(1)) adder_4 (.a(Q[3]), .b(FunSel[1]), .out(adder_1_out[3]), .cin(adder_3_cout), .cout(adder_4_cout));
  Adder #(.width(1)) adder_5 (.a(Q[4]), .b(FunSel[1]), .out(adder_1_out[4]), .cin(adder_4_cout), .cout(adder_5_cout));
  Adder #(.width(1)) adder_6 (.a(Q[5]), .b(FunSel[1]), .out(adder_1_out[5]), .cin(adder_5_cout), .cout(adder_6_cout));
  Adder #(.width(1)) adder_7 (.a(Q[6]), .b(FunSel[1]), .out(adder_1_out[6]), .cin(adder_6_cout), .cout(adder_7_cout));
  Adder #(.width(1)) adder_8 (.a(Q[7]), .b(FunSel[1]), .out(adder_1_out[7]), .cin(adder_7_cout));  // open: cout
  Adder #(.width(1)) adder_9 (.a(Q[0]), .b(FunSel[0]), .out(adder_9_out[0]), .cout(adder_9_cout));  // open: cin
  Adder #(.width(1)) adder_10 (.a(Q[1]), .b(FunSel[1]), .out(adder_9_out[1]), .cin(adder_9_cout), .cout(adder_10_cout));
  Adder #(.width(1)) adder_11 (
    .a(Q[2]), .b(FunSel[1]), .out(adder_9_out[2]), .cin(adder_10_cout), .cout(adder_11_cout));
  Adder #(.width(1)) adder_12 (
    .a(Q[3]), .b(FunSel[1]), .out(adder_9_out[3]), .cin(adder_11_cout), .cout(adder_12_cout));
  Adder #(.width(1)) adder_13 (
    .a(Q[4]), .b(FunSel[1]), .out(adder_9_out[4]), .cin(adder_12_cout), .cout(adder_13_cout));
  Adder #(.width(1)) adder_14 (
    .a(Q[5]), .b(FunSel[1]), .out(adder_9_out[5]), .cin(adder_13_cout), .cout(adder_14_cout));
  Adder #(.width(1)) adder_15 (
    .a(Q[6]), .b(FunSel[1]), .out(adder_9_out[6]), .cin(adder_14_cout), .cout(adder_15_cout));
  Adder #(.width(1)) adder_16 (.a(Q[7]), .b(FunSel[1]), .out(adder_9_out[7]), .cin(adder_15_cout));  // open: cout
  Multiplexer #(.select(2), .width(8)) multiplexer_1 (
    .in0(Clear), .in1(adder_9_out), .in2(adder_1_out), .in3(Load), .out(multiplexer_1_out), .sel(FunSel),
    .en(E));
  Clock clock_1 ();  // open: out
  D_Flip_Flop d_ff_1 (.clk(Clock), .D(multiplexer_1_out[0]), .Q(Q[0]));  // open: Qn, preset, en, reset
  D_Flip_Flop d_ff_2 (.clk(Clock), .D(multiplexer_1_out[1]), .Q(Q[1]));  // open: Qn, preset, en, reset
  D_Flip_Flop d_ff_3 (.clk(Clock), .D(multiplexer_1_out[2]), .Q(Q[2]));  // open: Qn, preset, en, reset
  D_Flip_Flop d_ff_4 (.clk(Clock), .D(multiplexer_1_out[3]), .Q(Q[3]));  // open: Qn, preset, en, reset
  D_Flip_Flop d_ff_5 (.clk(Clock), .D(multiplexer_1_out[4]), .Q(Q[4]));  // open: Qn, preset, en, reset
  D_Flip_Flop d_ff_6 (.clk(Clock), .D(multiplexer_1_out[5]), .Q(Q[5]));  // open: Qn, preset, en, reset
  D_Flip_Flop d_ff_7 (.clk(Clock), .D(multiplexer_1_out[6]), .Q(Q[6]));  // open: Qn, preset, en, reset
  D_Flip_Flop d_ff_8 (.clk(Clock), .D(multiplexer_1_out[7]), .Q(Q[7]));  // open: Qn, preset, en, reset
endmodule

module _16_bit_Register (
  input  [15:0] Clear,
  input  [15:0] Load,
  input  [1:0] FunSel,
  input  Clock,
  input  E,
  output [15:0] Q
);

  wire adder_1_cout, adder_2_cout, adder_3_cout, adder_4_cout, adder_5_cout, adder_6_cout, adder_7_cout,
       adder_8_cout, adder_9_cout, adder_10_cout, adder_11_cout, adder_12_cout, adder_13_cout, adder_14_cout,
       adder_15_cout, adder_17_cout, adder_18_cout, adder_19_cout, adder_20_cout, adder_21_cout,
       adder_22_cout, adder_23_cout, adder_25_cout, adder_26_cout, adder_27_cout, adder_28_cout,
       adder_29_cout, adder_30_cout, adder_31_cout;
  wire [15:0] adder_1_out, adder_17_out, multiplexer_1_out;

  Adder #(.width(1)) adder_1 (.a(Q[0]), .b(FunSel[1]), .out(adder_1_out[0]), .cout(adder_1_cout));  // open: cin
  Adder #(.width(1)) adder_2 (.a(Q[1]), .b(FunSel[1]), .out(adder_1_out[1]), .cin(adder_1_cout), .cout(adder_2_cout));
  Adder #(.width(1)) adder_3 (.a(Q[2]), .b(FunSel[1]), .out(adder_1_out[2]), .cin(adder_2_cout), .cout(adder_3_cout));
  Adder #(.width(1)) adder_4 (.a(Q[3]), .b(FunSel[1]), .out(adder_1_out[3]), .cin(adder_3_cout), .cout(adder_4_cout));
  Adder #(.width(1)) adder_5 (.a(Q[4]), .b(FunSel[1]), .out(adder_1_out[4]), .cin(adder_4_cout), .cout(adder_5_cout));
  Adder #(.width(1)) adder_6 (.a(Q[5]), .b(FunSel[1]), .out(adder_1_out[5]), .cin(adder_5_cout), .cout(adder_6_cout));
  Adder #(.width(1)) adder_7 (.a(Q[6]), .b(FunSel[1]), .out(adder_1_out[6]), .cin(adder_6_cout), .cout(adder_7_cout));
  Adder #(.width(1)) adder_8 (.a(Q[7]), .b(FunSel[1]), .out(adder_1_out[7]), .cin(adder_7_cout), .cout(adder_8_cout));
  Adder #(.width(1)) adder_9 (.a(Q[8]), .b(FunSel[1]), .out(adder_1_out[8]), .cin(adder_8_cout), .cout(adder_9_cout));
  Adder #(.width(1)) adder_10 (.a(Q[9]), .b(FunSel[1]), .out(adder_1_out[9]), .cin(adder_9_cout), .cout(adder_10_cout));
  Adder #(.width(1)) adder_11 (
    .a(Q[10]), .b(FunSel[1]), .out(adder_1_out[10]), .cin(adder_10_cout), .cout(adder_11_cout));
  Adder #(.width(1)) adder_12 (
    .a(Q[11]), .b(FunSel[1]), .out(adder_1_out[11]), .cin(adder_11_cout), .cout(adder_12_cout));
  Adder #(.width(1)) adder_13 (
    .a(Q[12]), .b(FunSel[1]), .out(adder_1_out[12]), .cin(adder_12_cout), .cout(adder_13_cout));
  Adder #(.width(1)) adder_14 (
    .a(Q[13]), .b(FunSel[1]), .out(adder_1_out[13]), .cin(adder_13_cout), .cout(adder_14_cout));
  Adder #(.width(1)) adder_15 (
    .a(Q[14]), .b(FunSel[1]), .out(adder_1_out[14]), .cin(adder_14_cout), .cout(adder_15_cout));
  Adder #(.width(1)) adder_16 (.a(Q[15]), .b(FunSel[1]), .out(adder_1_out[15]), .cin(adder_15_cout));  // open: cout
  Adder #(.width(1)) adder_17 (.a(Q[0]), .b(FunSel[0]), .out(adder_17_out[0]), .cout(adder_17_cout));  // open: cin
  Adder #(.width(1)) adder_18 (
    .a(Q[1]), .b(FunSel[1]), .out(adder_17_out[1]), .cin(adder_17_cout), .cout(adder_18_cout));
  Adder #(.width(1)) adder_19 (
    .a(Q[2]), .b(FunSel[1]), .out(adder_17_out[2]), .cin(adder_18_cout), .cout(adder_19_cout));
  Adder #(.width(1)) adder_20 (
    .a(Q[3]), .b(FunSel[1]), .out(adder_17_out[3]), .cin(adder_19_cout), .cout(adder_20_cout));
  Adder #(.width(1)) adder_21 (
    .a(Q[4]), .b(FunSel[1]), .out(adder_17_out[4]), .cin(adder_20_cout), .cout(adder_21_cout));
  Adder #(.width(1)) adder_22 (
    .a(Q[5]), .b(FunSel[1]), .out(adder_17_out[5]), .cin(adder_21_cout), .cout(adder_22_cout));
  Adder #(.width(1)) adder_23 (
    .a(Q[6]), .b(FunSel[1]), .out(adder_17_out[6]), .cin(adder_22_cout), .cout(adder_23_cout));
  Adder #(.width(1)) adder_24 (.a(Q[7]), .b(FunSel[1]), .out(adder_17_out[7]), .cin(adder_23_cout));  // open: cout
  Adder #(.width(1)) adder_25 (.a(Q[8]), .b(FunSel[1]), .out(adder_17_out[8]), .cout(adder_25_cout));  // open: cin
  Adder #(.width(1)) adder_26 (
    .a(Q[9]), .b(FunSel[1]), .out(adder_17_out[9]), .cin(adder_25_cout), .cout(adder_26_cout));
  Adder #(.width(1)) adder_27 (
    .a(Q[10]), .b(FunSel[1]), .out(adder_17_out[10]), .cin(adder_26_cout), .cout(adder_27_cout));
  Adder #(.width(1)) adder_28 (
    .a(Q[11]), .b(FunSel[1]), .out(adder_17_out[11]), .cin(adder_27_cout), .cout(adder_28_cout));
  Adder #(.width(1)) adder_29 (
    .a(Q[12]), .b(FunSel[1]), .out(adder_17_out[12]), .cin(adder_28_cout), .cout(adder_29_cout));
  Adder #(.width(1)) adder_30 (
    .a(Q[13]), .b(FunSel[1]), .out(adder_17_out[13]), .cin(adder_29_cout), .cout(adder_30_cout));
  Adder #(.width(1)) adder_31 (
    .a(Q[14]), .b(FunSel[1]), .out(adder_17_out[14]), .cin(adder_30_cout), .cout(adder_31_cout));
  Adder #(.width(1)) adder_32 (.a(Q[15]), .b(FunSel[1]), .out(adder_17_out[15]), .cin(adder_31_cout));  // open: cout
  Multiplexer #(.select(2), .width(16)) multiplexer_1 (
    .in0(Clear), .in1(adder_17_out), .in2(adder_1_out), .in3(Load), .out(multiplexer_1_out), .sel(FunSel),
    .en(E));
  Clock clock_1 ();  // open: out
  D_Flip_Flop d_ff_1 (.clk(Clock), .D(multiplexer_1_out[0]), .Q(Q[0]));  // open: Qn, preset, en, reset
  D_Flip_Flop d_ff_2 (.clk(Clock), .D(multiplexer_1_out[1]), .Q(Q[1]));  // open: Qn, preset, en, reset
  D_Flip_Flop d_ff_3 (.clk(Clock), .D(multiplexer_1_out[2]), .Q(Q[2]));  // open: Qn, preset, en, reset
  D_Flip_Flop d_ff_4 (.clk(Clock), .D(multiplexer_1_out[3]), .Q(Q[3]));  // open: Qn, preset, en, reset
  D_Flip_Flop d_ff_5 (.clk(Clock), .D(multiplexer_1_out[4]), .Q(Q[4]));  // open: Qn, preset, en, reset
  D_Flip_Flop d_ff_6 (.clk(Clock), .D(multiplexer_1_out[5]), .Q(Q[5]));  // open: Qn, preset, en, reset
  D_Flip_Flop d_ff_7 (.clk(Clock), .D(multiplexer_1_out[6]), .Q(Q[6]));  // open: Qn, preset, en, reset
  D_Flip_Flop d_ff_8 (.clk(Clock), .D(multiplexer_1_out[7]), .Q(Q[7]));  // open: Qn, preset, en, reset
  D_Flip_Flop d_ff_9 (.clk(Clock), .D(multiplexer_1_out[8]), .Q(Q[8]));  // open: Qn, preset, en, reset
  D_Flip_Flop d_ff_10 (.clk(Clock), .D(multiplexer_1_out[9]), .Q(Q[9]));  // open: Qn, preset, en, reset
  D_Flip_Flop d_ff_11 (.clk(Clock), .D(multiplexer_1_out[10]), .Q(Q[10]));  // open: Qn, preset, en, reset
  D_Flip_Flop d_ff_12 (.clk(Clock), .D(multiplexer_1_out[11]), .Q(Q[11]));  // open: Qn, preset, en, reset
  D_Flip_Flop d_ff_13 (.clk(Clock), .D(multiplexer_1_out[12]), .Q(Q[12]));  // open: Qn, preset, en, reset
  D_Flip_Flop d_ff_14 (.clk(Clock), .D(multiplexer_1_out[13]), .Q(Q[13]));  // open: Qn, preset, en, reset
  D_Flip_Flop d_ff_15 (.clk(Clock), .D(multiplexer_1_out[14]), .Q(Q[14]));  // open: Qn, preset, en, reset
  D_Flip_Flop d_ff_16 (.clk(Clock), .D(multiplexer_1_out[15]), .Q(Q[15]));  // open: Qn, preset, en, reset
endmodule

module Part_2a (
  input  [7:0] Clear,
  input  [7:0] Load,
  input  E,
  input  in_4,
  input  [1:0] FunSel,
  input  [3:0] RegSel,
  input  [1:0] OutASel,
  input  [1:0] OutBSel,
  output [7:0] OutA,
  output [7:0] OutB
);

  wire [7:0] n8_bit_register_1_q, n8_bit_register_2_q, n8_bit_register_3_q, R0_q;

  _8_bit_Register R0 (.Clear(Clear), .Load(Load), .Clock(in_4), .FunSel(FunSel), .E(RegSel[3]), .Q(R0_q));
  _8_bit_Register u_8_bit_register_1 (
    .Clear(Clear), .Load(Load), .Clock(in_4), .FunSel(FunSel), .E(RegSel[2]), .Q(n8_bit_register_1_q));
  _8_bit_Register u_8_bit_register_2 (
    .Clear(Clear), .Load(Load), .Clock(in_4), .FunSel(FunSel), .E(RegSel[1]), .Q(n8_bit_register_2_q));
  _8_bit_Register u_8_bit_register_3 (
    .Clear(Clear), .Load(Load), .Clock(in_4), .FunSel(FunSel), .E(RegSel[0]), .Q(n8_bit_register_3_q));
  Multiplexer #(.select(2), .width(8)) multiplexer_1 (
    .in0(R0_q), .in1(n8_bit_register_1_q), .in2(n8_bit_register_2_q), .in3(n8_bit_register_3_q), .out(OutA),
    .sel(OutASel), .en(E));
  Multiplexer #(.select(2), .width(8)) multiplexer_2 (
    .in0(R0_q), .in1(n8_bit_register_1_q), .in2(n8_bit_register_2_q), .in3(n8_bit_register_3_q), .out(OutB),
    .sel(OutBSel), .en(E));
endmodule

module Part_2b (
  input  [7:0] Clear,
  input  [7:0] Load,
  input  E,
  input  in_4,
  input  [1:0] FunSel,
  input  [2:0] RegSel,
  input  [1:0] OutCSel,
  output [7:0] OutC
);

  wire [7:0] AR_q, PC_q, SP_q;

  _8_bit_Register PC (.Clear(Clear), .Load(Load), .Clock(in_4), .FunSel(FunSel), .E(RegSel[2]), .Q(PC_q));
  _8_bit_Register AR (.Clear(Clear), .Load(Load), .Clock(in_4), .FunSel(FunSel), .E(RegSel[1]), .Q(AR_q));
  _8_bit_Register SP (.Clear(Clear), .Load(Load), .Clock(in_4), .FunSel(FunSel), .E(RegSel[0]), .Q(SP_q));
  Multiplexer #(.select(2), .width(8)) multiplexer_1 (
    .in0(PC_q), .in1(PC_q), .in2(AR_q), .in3(SP_q), .out(OutC), .sel(OutCSel), .en(E));
endmodule
