// Logisim project corgproje2.circ as structural Verilog: 15 circuits, main circuit Project1-part-2c
module Project1_part_2c (
  input  [7:0] Load,
  input  L_H,
  input  [15:0] Clear,
  input  [1:0] FunSel,
  input  Clock,
  input  E,
  output [7:0] IR_07,
  output [15:0] Q,
  output [7:0] IR_815
);

  wire adder_1_cout, adder_2_cout, adder_3_cout, adder_4_cout, adder_5_cout, adder_6_cout, adder_7_cout,
       adder_8_cout, adder_9_cout, adder_10_cout, adder_11_cout, adder_12_cout, adder_13_cout, adder_14_cout,
       adder_15_cout, adder_17_cout, adder_18_cout, adder_19_cout, adder_20_cout, adder_21_cout,
       adder_22_cout, adder_23_cout, adder_25_cout, adder_26_cout, adder_27_cout, adder_28_cout,
       adder_29_cout, adder_30_cout, adder_31_cout;
  wire [15:0] adder_1_out, adder_17_out, multiplexer_1_out, multiplexer_2_out;

  Adder #(.width(1)) adder_1 (.a(IR_07[0]), .b(FunSel[1]), .out(adder_1_out[0]), .cout(adder_1_cout));  // open: cin
  Adder #(.width(1)) adder_2 (
    .a(IR_07[1]), .b(FunSel[1]), .out(adder_1_out[1]), .cin(adder_1_cout), .cout(adder_2_cout));
  Adder #(.width(1)) adder_3 (
    .a(IR_07[2]), .b(FunSel[1]), .out(adder_1_out[2]), .cin(adder_2_cout), .cout(adder_3_cout));
  Adder #(.width(1)) adder_4 (
    .a(IR_07[3]), .b(FunSel[1]), .out(adder_1_out[3]), .cin(adder_3_cout), .cout(adder_4_cout));
  Adder #(.width(1)) adder_5 (
    .a(IR_07[4]), .b(FunSel[1]), .out(adder_1_out[4]), .cin(adder_4_cout), .cout(adder_5_cout));
  Adder #(.width(1)) adder_6 (
    .a(IR_07[5]), .b(FunSel[1]), .out(adder_1_out[5]), .cin(adder_5_cout), .cout(adder_6_cout));
  Adder #(.width(1)) adder_7 (
    .a(IR_07[6]), .b(FunSel[1]), .out(adder_1_out[6]), .cin(adder_6_cout), .cout(adder_7_cout));
  Adder #(.width(1)) adder_8 (
    .a(IR_07[7]), .b(FunSel[1]), .out(adder_1_out[7]), .cin(adder_7_cout), .cout(adder_8_cout));
  Adder #(.width(1)) adder_9 (
    .a(IR_815[0]), .b(FunSel[1]), .out(adder_1_out[8]), .cin(adder_8_cout), .cout(adder_9_cout));
  Adder #(.width(1)) adder_10 (
    .a(IR_815[1]), .b(FunSel[1]), .out(adder_1_out[9]), .cin(adder_9_cout), .cout(adder_10_cout));
  Adder #(.width(1)) adder_11 (
    .a(IR_815[2]), .b(FunSel[1]), .out(adder_1_out[10]), .cin(adder_10_cout), .cout(adder_11_cout));
  Adder #(.width(1)) adder_12 (
    .a(IR_815[3]), .b(FunSel[1]), .out(adder_1_out[11]), .cin(adder_11_cout), .cout(adder_12_cout));
  Adder #(.width(1)) adder_13 (
    .a(IR_815[4]), .b(FunSel[1]), .out(adder_1_out[12]), .cin(adder_12_cout), .cout(adder_13_cout));
  Adder #(.width(1)) adder_14 (
    .a(IR_815[5]), .b(FunSel[1]), .out(adder_1_out[13]), .cin(adder_13_cout), .cout(adder_14_cout));
  Adder #(.width(1)) adder_15 (
    .a(IR_815[6]), .b(FunSel[1]), .out(adder_1_out[14]), .cin(adder_14_cout), .cout(adder_15_cout));
  Adder #(.width(1)) adder_16 (.a(IR_815[7]), .b(FunSel[1]), .out(adder_1_out[15]), .cin(adder_15_cout));  // open: cout
  Adder #(.width(1)) adder_17 (.a(IR_07[0]), .b(FunSel[0]), .out(adder_17_out[0]), .cout(adder_17_cout));  // open: cin
  Adder #(.width(1)) adder_18 (
    .a(IR_07[1]), .b(FunSel[1]), .out(adder_17_out[1]), .cin(adder_17_cout), .cout(adder_18_cout));
  Adder #(.width(1)) adder_19 (
    .a(IR_07[2]), .b(FunSel[1]), .out(adder_17_out[2]), .cin(adder_18_cout), .cout(adder_19_cout));
  Adder #(.width(1)) adder_20 (
    .a(IR_07[3]), .b(FunSel[1]), .out(adder_17_out[3]), .cin(adder_19_cout), .cout(adder_20_cout));
  Adder #(.width(1)) adder_21 (
    .a(IR_07[4]), .b(FunSel[1]), .out(adder_17_out[4]), .cin(adder_20_cout), .cout(adder_21_cout));
  Adder #(.width(1)) adder_22 (
    .a(IR_07[5]), .b(FunSel[1]), .out(adder_17_out[5]), .cin(adder_21_cout), .cout(adder_22_cout));
  Adder #(.width(1)) adder_23 (
    .a(IR_07[6]), .b(FunSel[1]), .out(adder_17_out[6]), .cin(adder_22_cout), .cout(adder_23_cout));
  Adder #(.width(1)) adder_24 (.a(IR_07[7]), .b(FunSel[1]), .out(adder_17_out[7]), .cin(adder_23_cout));  // open: cout
  Adder #(.width(1)) adder_25 (.a(IR_815[0]), .b(FunSel[1]), .out(adder_17_out[8]), .cout(adder_25_cout));  // open: cin
  Adder #(.width(1)) adder_26 (
    .a(IR_815[1]), .b(FunSel[1]), .out(adder_17_out[9]), .cin(adder_25_cout), .cout(adder_26_cout));
  Adder #(.width(1)) adder_27 (
    .a(IR_815[2]), .b(FunSel[1]), .out(adder_17_out[10]), .cin(adder_26_cout), .cout(adder_27_cout));
  Adder #(.width(1)) adder_28 (
    .a(IR_815[3]), .b(FunSel[1]), .out(adder_17_out[11]), .cin(adder_27_cout), .cout(adder_28_cout));
  Adder #(.width(1)) adder_29 (
    .a(IR_815[4]), .b(FunSel[1]), .out(adder_17_out[12]), .cin(adder_28_cout), .cout(adder_29_cout));
  Adder #(.width(1)) adder_30 (
    .a(IR_815[5]), .b(FunSel[1]), .out(adder_17_out[13]), .cin(adder_29_cout), .cout(adder_30_cout));
  Adder #(.width(1)) adder_31 (
    .a(IR_815[6]), .b(FunSel[1]), .out(adder_17_out[14]), .cin(adder_30_cout), .cout(adder_31_cout));
  Adder #(.width(1)) adder_32 (
    .a(IR_815[7]), .b(FunSel[1]), .out(adder_17_out[15]), .cin(adder_31_cout));  // open: cout
  Multiplexer #(.width(16), .enable("false")) multiplexer_1 (
    .in0({Load, IR_07}), .in1({IR_815, Load}), .out(multiplexer_1_out), .sel(L_H));
  Multiplexer #(.select(2), .width(16)) multiplexer_2 (
    .in0(Clear), .in1(adder_17_out), .in2(adder_1_out), .in3(multiplexer_1_out), .out(multiplexer_2_out),
    .sel(FunSel), .en(E));
  Clock clock_1 ();  // open: out
  D_Flip_Flop d_ff_1 (.clk(Clock), .D(multiplexer_2_out[0]), .Q(IR_07[0]));  // open: Qn, preset, en, reset
  D_Flip_Flop d_ff_2 (.clk(Clock), .D(multiplexer_2_out[1]), .Q(IR_07[1]));  // open: Qn, preset, en, reset
  D_Flip_Flop d_ff_3 (.clk(Clock), .D(multiplexer_2_out[2]), .Q(IR_07[2]));  // open: Qn, preset, en, reset
  D_Flip_Flop d_ff_4 (.clk(Clock), .D(multiplexer_2_out[3]), .Q(IR_07[3]));  // open: Qn, preset, en, reset
  D_Flip_Flop d_ff_5 (.clk(Clock), .D(multiplexer_2_out[4]), .Q(IR_07[4]));  // open: Qn, preset, en, reset
  D_Flip_Flop d_ff_6 (.clk(Clock), .D(multiplexer_2_out[5]), .Q(IR_07[5]));  // open: Qn, preset, en, reset
  D_Flip_Flop d_ff_7 (.clk(Clock), .D(multiplexer_2_out[6]), .Q(IR_07[6]));  // open: Qn, preset, en, reset
  D_Flip_Flop d_ff_8 (.clk(Clock), .D(multiplexer_2_out[7]), .Q(IR_07[7]));  // open: Qn, preset, en, reset
  D_Flip_Flop d_ff_9 (.clk(Clock), .D(multiplexer_2_out[8]), .Q(IR_815[0]));  // open: Qn, preset, en, reset
  D_Flip_Flop d_ff_10 (.clk(Clock), .D(multiplexer_2_out[9]), .Q(IR_815[1]));  // open: Qn, preset, en, reset
  D_Flip_Flop d_ff_11 (.clk(Clock), .D(multiplexer_2_out[10]), .Q(IR_815[2]));  // open: Qn, preset, en, reset
  D_Flip_Flop d_ff_12 (.clk(Clock), .D(multiplexer_2_out[11]), .Q(IR_815[3]));  // open: Qn, preset, en, reset
  D_Flip_Flop d_ff_13 (.clk(Clock), .D(multiplexer_2_out[12]), .Q(IR_815[4]));  // open: Qn, preset, en, reset
  D_Flip_Flop d_ff_14 (.clk(Clock), .D(multiplexer_2_out[13]), .Q(IR_815[5]));  // open: Qn, preset, en, reset
  D_Flip_Flop d_ff_15 (.clk(Clock), .D(multiplexer_2_out[14]), .Q(IR_815[6]));  // open: Qn, preset, en, reset
  D_Flip_Flop d_ff_16 (.clk(Clock), .D(multiplexer_2_out[15]), .Q(IR_815[7]));  // open: Qn, preset, en, reset

  assign Q = {IR_815, IR_07};
endmodule

module Project1_8_bit_Register (
  input  [7:0] Clear,
  input  [7:0] Load,
  input  Clock,
  input  [1:0] FunSel,
  input  E,
  output [7:0] Q
);

  wire adder_1_cout, adder_2_cout, adder_3_cout, adder_4_cout, adder_5_cout, adder_6_cout, adder_7_cout,
       adder_9_cout, adder_10_cout, adder_11_cout, adder_12_cout, adder_13_cout, adder_14_cout, adder_15_cout;
  wire [7:0] adder_1_out, adder_9_out, multiplexer_1_out;

  Adder #(.width(1)) adder_1 (.a(Q[0]), .b(FunSel[1]), .out(adder_1_out[0]), .cout(adder_1_cout));  // open: cin
  Adder #(.width(1)) adder_2 (.a(Q[1]), .b(FunSel[1]), .out(adder_1_out[1]), .cin(adder_1_cout), .cout(adder_2_cout));
  Adder #(.width(1)) adder_3 (.a(Q[2]), .b(FunSel[1]), .out(adder_1_out[2]), .cin(adder_2_cout), .cout(adder_3_cout));
  Adder #(.width(1)) adder_4 (.a(Q[3]), .b(FunSel[1]), .out(adder_1_out[3]), .cin(adder_3_cout), .cout(adder_4_cout));
  Adder #(.width(1)) adder_5 (.a(Q[4]), .b(FunSel[1]), .out(adder_1_out[4]), .cin(adder_4_cout), .cout(adder_5_cout));
  Adder #(.width(1)) adder_6 (.a(Q[5]), .b(FunSel[1]), .out(adder_1_out[5]), .cin(adder_5_cout), .cout(adder_6_cout));
  Adder #(.width(1)) adder_7 (.a(Q[6]), .b(FunSel[1]), .out(adder_1_out[6]), .cin(adder_6_cout), .cout(adder_7_cout));
  Adder #(.width(1)) adder_8 (.a(Q[7]), .b(FunSel[1]), .out(adder_1_out[7]), .cin(adder_7_cout));  // open: cout
  Adder #(.width(1)) adder_9 (.a(Q[0]), .b(FunSel[0]), .out(adder_9_out[0]), .cout(adder_9_cout));  // open: cin
  Adder #(.width(1)) adder_10 (.a(Q[1]), .b(FunSel[1]), .out(adder_9_out[1]), .cin(adder_9_cout), .cout(adder_10_cout));
  Adder #(.width(1)) adder_11 (
    .a(Q[2]), .b(FunSel[1]), .out(adder_9_out[2]), .cin(adder_10_cout), .cout(adder_11_cout));
  Adder #(.width(1)) adder_12 (
    .a(Q[3]), .b(FunSel[1]), .out(adder_9_out[3]), .cin(adder_11_cout), .cout(adder_12_cout));
  Adder #(.width(1)) adder_13 (
    .a(Q[4]), .b(FunSel[1]), .out(adder_9_out[4]), .cin(adder_12_cout), .cout(adder_13_cout));
  Adder #(.width(1)) adder_14 (
    .a(Q[5]), .b(FunSel[1]), .out(adder_9_out[5]), .cin(adder_13_cout), .cout(adder_14_cout));
  Adder #(.width(1)) adder_15 (
    .a(Q[6]), .b(FunSel[1]), .out(adder_9_out[6]), .cin(adder_14_cout), .cout(adder_15_cout));
  Adder #(.width(1)) adder_16 (.a(Q[7]), .b(FunSel[1]), .out(adder_9_out[7]), .cin(adder_15_cout));  // open: cout
  Multiplexer #(.select(2), .width(8)) multiplexer_1 (
    .in0(Clear), .in1(adder_9_out), .in2(adder_1_out), .in3(Load), .out(multiplexer_1_out), .sel(FunSel),
    .en(E));
  Clock clock_1 ();  // open: out
  D_Flip_Flop d_ff_1 (.clk(Clock), .D(multiplexer_1_out[0]), .Q(Q[0]));  // open: Qn, preset, en, reset
  D_Flip_Flop d_ff_2 (.clk(Clock), .D(multiplexer_1_out[1]), .Q(Q[1]));  // open: Qn, preset, en, reset
  D_Flip_Flop d_ff_3 (.clk(Clock), .D(multiplexer_1_out[2]), .Q(Q[2]));  // open: Qn, preset, en, reset
  D_Flip_Flop d_ff_4 (.clk(Clock), .D(multiplexer_1_out[3]), .Q(Q[3]));  // open: Qn, preset, en, reset
  D_Flip_Flop d_ff_5 (.clk(Clock), .D(multiplexer_1_out[4]), .Q(Q[4]));  // open: Qn, preset, en, reset
  D_Flip_Flop d_ff_6 (.clk(Clock), .D(multiplexer_1_out[5]), .Q(Q[5]));  // open: Qn, preset, en, reset
  D_Flip_Flop d_ff_7 (.clk(Clock), .D(multiplexer_1_out[6]), .Q(Q[6]));  // open: Qn, preset, en, reset
  D_Flip_Flop d_ff_8 (.clk(Clock), .D(multiplexer_1_out[7]), .Q(Q[7]));  // open: Qn, preset, en, reset
endmodule

module Project1_16_bit_Register (
  input  [15:0] Clear,
  input  [15:0] Load,
  input  [1:0] FunSel,
  input  Clock,
  input  E,
  output [15:0] Q
);

  wire adder_1_cout, adder_2_cout, adder_3_cout, adder_4_cout, adder_5_cout, adder_6_cout, adder_7_cout,
       adder_8_cout, adder_9_cout, adder_10_cout, adder_11_cout, adder_12_cout, adder_13_cout, adder_14_cout,
       adder_15_cout, adder_17_cout, adder_18_cout, adder_19_cout, adder_20_cout, adder_21_cout,
       adder_22_cout, adder_23_cout, adder_25_cout, adder_26_cout, adder_27_cout, adder_28_cout,
       adder_29_cout, adder_30_cout, adder_31_cout;
  wire [15:0] adder_1_out, adder_17_out, multiplexer_1_out;

  Adder #(.width(1)) adder_1 (.a(Q[0]), .b(FunSel[1]), .out(adder_1_out[0]), .cout(adder_1_cout));  // open: cin
  Adder #(.width(1)) adder_2 (.a(Q[1]), .b(FunSel[1]), .out(adder_1_out[1]), .cin(adder_1_cout), .cout(adder_2_cout));
  Adder #(.width(1)) adder_3 (.a(Q[2]), .b(FunSel[1]), .out(adder_1_out[2]), .cin(adder_2_cout), .cout(adder_3_cout));
  Adder #(.width(1)) adder_4 (.a(Q[3]), .b(FunSel[1]), .out(adder_1_out[3]), .cin(adder_3_cout), .cout(adder_4_cout));
  Adder #(.width(1)) adder_5 (.a(Q[4]), .b(FunSel[1]), .out(adder_1_out[4]), .cin(adder_4_cout), .cout(adder_5_cout));
  Adder #(.width(1)) adder_6 (.a(Q[5]), .b(FunSel[1]), .out(adder_1_out[5]), .cin(adder_5_cout), .cout(adder_6_cout));
  Adder #(.width(1)) adder_7 (.a(Q[6]), .b(FunSel[1]), .out(adder_1_out[6]), .cin(adder_6_cout), .cout(adder_7_cout));
  Adder #(.width(1)) adder_8 (.a(Q[7]), .b(FunSel[1]), .out(adder_1_out[7]), .cin(adder_7_cout), .cout(adder_8_cout));
  Adder #(.width(1)) adder_9 (.a(Q[8]), .b(FunSel[1]), .out(adder_1_out[8]), .cin(adder_8_cout), .cout(adder_9_cout));
  Adder #(.width(1)) adder_10 (.a(Q[9]), .b(FunSel[1]), .out(adder_1_out[9]), .cin(adder_9_cout), .cout(adder_10_cout));
  Adder #(.width(1)) adder_11 (
    .a(Q[10]), .b(FunSel[1]), .out(adder_1_out[10]), .cin(adder_10_cout), .cout(adder_11_cout));
  Adder #(.width(1)) adder_12 (
    .a(Q[11]), .b(FunSel[1]), .out(adder_1_out[11]), .cin(adder_11_cout), .cout(adder_12_cout));
  Adder #(.width(1)) adder_13 (
    .a(Q[12]), .b(FunSel[1]), .out(adder_1_out[12]), .cin(adder_12_cout), .cout(adder_13_cout));
  Adder #(.width(1)) adder_14 (
    .a(Q[13]), .b(FunSel[1]), .out(adder_1_out[13]), .cin(adder_13_cout), .cout(adder_14_cout));
  Adder #(.width(1)) adder_15 (
    .a(Q[14]), .b(FunSel[1]), .out(adder_1_out[14]), .cin(adder_14_cout), .cout(adder_15_cout));
  Adder #(.width(1)) adder_16 (.a(Q[15]), .b(FunSel[1]), .out(adder_1_out[15]), .cin(adder_15_cout));  // open: cout
  Adder #(.width(1)) adder_17 (.a(Q[0]), .b(FunSel[0]), .out(adder_17_out[0]), .cout(adder_17_cout));  // open: cin
  Adder #(.width(1)) adder_18 (
    .a(Q[1]), .b(FunSel[1]), .out(adder_17_out[1]), .cin(adder_17_cout), .cout(adder_18_cout));
  Adder #(.width(1)) adder_19 (
    .a(Q[2]), .b(FunSel[1]), .out(adder_17_out[2]), .cin(adder_18_cout), .cout(adder_19_cout));
  Adder #(.width(1)) adder_20 (
    .a(Q[3]), .b(FunSel[1]), .out(adder_17_out[3]), .cin(adder_19_cout), .cout(adder_20_cout));
  Adder #(.width(1)) adder_21 (
    .a(Q[4]), .b(FunSel[1]), .out(adder_17_out[4]), .cin(adder_20_cout), .cout(adder_21_cout));
  Adder #(.width(1)) adder_22 (
    .a(Q[5]), .b(FunSel[1]), .out(adder_17_out[5]), .cin(adder_21_cout), .cout(adder_22_cout));
  Adder #(.width(1)) adder_23 (
    .a(Q[6]), .b(FunSel[1]), .out(adder_17_out[6]), .cin(adder_22_cout), .cout(adder_23_cout));
  Adder #(.width(1)) adder_24 (.a(Q[7]), .b(FunSel[1]), .out(adder_17_out[7]), .cin(adder_23_cout));  // open: cout
  Adder #(.width(1)) adder_25 (.a(Q[8]), .b(FunSel[1]), .out(adder_17_out[8]), .cout(adder_25_cout));  // open: cin
  Adder #(.width(1)) adder_26 (
    .a(Q[9]), .b(FunSel[1]), .out(adder_17_out[9]), .cin(adder_25_cout), .cout(adder_26_cout));
  Adder #(.width(1)) adder_27 (
    .a(Q[10]), .b(FunSel[1]), .out(adder_17_out[10]), .cin(adder_26_cout), .cout(adder_27_cout));
  Adder #(.width(1)) adder_28 (
    .a(Q[11]), .b(FunSel[1]), .out(adder_17_out[11]), .cin(adder_27_cout), .cout(adder_28_cout));
  Adder #(.width(1)) adder_29 (
    .a(Q[12]), .b(FunSel[1]), .out(adder_17_out[12]), .cin(adder_28_cout), .cout(adder_29_cout));
  Adder #(.width(1)) adder_30 (
    .a(Q[13]), .b(FunSel[1]), .out(adder_17_out[13]), .cin(adder_29_cout), .cout(adder_30_cout));
  Adder #(.width(1)) adder_31 (
    .a(Q[14]), .b(FunSel[1]), .out(adder_17_out[14]), .cin(adder_30_cout), .cout(adder_31_cout));
  Adder #(.width(1)) adder_32 (.a(Q[15]), .b(FunSel[1]), .out(adder_17_out[15]), .cin(adder_31_cout));  // open: cout
  Multiplexer #(.select(2), .width(16)) multiplexer_1 (
    .in0(Clear), .in1(adder_17_out), .in2(adder_1_out), .in3(Load), .out(multiplexer_1_out), .sel(FunSel),
    .en(E));
  Clock clock_1 ();  // open: out
  D_Flip_Flop d_ff_1 (.clk(Clock), .D(multiplexer_1_out[0]), .Q(Q[0]));  // open: Qn, preset, en, reset
  D_Flip_Flop d_ff_2 (.clk(Clock), .D(multiplexer_1_out[1]), .Q(Q[1]));  // open: Qn, preset, en, reset
  D_Flip_Flop d_ff_3 (.clk(Clock), .D(multiplexer_1_out[2]), .Q(Q[2]));  // open: Qn, preset, en, reset
  D_Flip_Flop d_ff_4 (.clk(Clock), .D(multiplexer_1_out[3]), .Q(Q[3]));  // open: Qn, preset, en, reset
  D_Flip_Flop d_ff_5 (.clk(Clock), .D(multiplexer_1_out[4]), .Q(Q[4]));  // open: Qn, preset, en, reset
  D_Flip_Flop d_ff_6 (.clk(Clock), .D(multiplexer_1_out[5]), .Q(Q[5]));  // open: Qn, preset, en, reset
  D_Flip_Flop d_ff_7 (.clk(Clock), .D(multiplexer_1_out[6]), .Q(Q[6]));  // open: Qn, preset, en, reset
  D_Flip_Flop d_ff_8 (.clk(Clock), .D(multiplexer_1_out[7]), .Q(Q[7]));  // open: Qn, preset, en, reset
  D_Flip_Flop d_ff_9 (.clk(Clock), .D(multiplexer_1_out[8]), .Q(Q[8]));  // open: Qn, preset, en, reset
  D_Flip_Flop d_ff_10 (.clk(Clock), .D(multiplexer_1_out[9]), .Q(Q[9]));  // open: Qn, preset, en, reset
  D_Flip_Flop d_ff_11 (.clk(Clock), .D(multiplexer_1_out[10]), .Q(Q[10]));  // open: Qn, preset, en, reset
  D_Flip_Flop d_ff_12 (.clk(Clock), .D(multiplexer_1_out[11]), .Q(Q[11]));  // open: Qn, preset, en, reset
  D_Flip_Flop d_ff_13 (.clk(Clock), .D(multiplexer_1_out[12]), .Q(Q[12]));  // open: Qn, preset, en, reset
  D_Flip_Flop d_ff_14 (.clk(Clock), .D(multiplexer_1_out[13]), .Q(Q[13]));  // open: Qn, preset, en, reset
  D_Flip_Flop d_ff_15 (.clk(Clock), .D(multiplexer_1_out[14]), .Q(Q[14]));  // open: Qn, preset, en, reset
  D_Flip_Flop d_ff_16 (.clk(Clock), .D(multiplexer_1_out[15]), .Q(Q[15]));  // open: Qn, preset, en, reset
endmodule

module Project1_Part_2a (
  input  [7:0] Clear,
  input  [7:0] Load,
  input  Clock,
  input  [1:0] FunSel,
  input  [3:0] RegSel,
  input  [1:0] OutASel,
  input  [1:0] OutBSel,
  output [7:0] OutA,
  output [7:0] OutB
);

  wire [7:0] project1_8_bit_register_1_q, project1_8_bit_register_2_q, project1_8_bit_register_3_q, R0_q;

  Project1_8_bit_Register R0 (.Clear(Clear), .Load(Load), .Clock(Clock), .FunSel(FunSel), .E(RegSel[3]), .Q(R0_q));
  Project1_8_bit_Register project1_8_bit_register_1 (
    .Clear(Clear), .Load(Load), .Clock(Clock), .FunSel(FunSel), .E(RegSel[2]), .Q(project1_8_bit_register_1_q));
  Project1_8_bit_Register project1_8_bit_register_2 (
    .Clear(Clear), .Load(Load), .Clock(Clock), .FunSel(FunSel), .E(RegSel[1]), .Q(project1_8_bit_register_2_q));
  Project1_8_bit_Register project1_8_bit_register_3 (
    .Clear(Clear), .Load(Load), .Clock(Clock), .FunSel(FunSel), .E(RegSel[0]), .Q(project1_8_bit_register_3_q));
  Multiplexer #(.select(2), .width(8), .enable("false")) multiplexer_1 (
    .in0(R0_q), .in1(project1_8_bit_register_1_q), .in2(project1_8_bit_register_2_q),
    .in3(project1_8_bit_register_3_q), .out(OutA), .sel(OutASel));
  Multiplexer #(.select(2), .width(8), .enable("false")) multiplexer_2 (
    .in0(R0_q), .in1(project1_8_bit_register_1_q), .in2(project1_8_bit_register_2_q),
    .in3(project1_8_bit_register_3_q), .out(OutB), .sel(OutBSel));
endmodule

module Project1_Part_2b (
  input  [7:0] Clear,
  input  [7:0] Load,
  input  Clock,
  input  [1:0] FunSel,
  input  [2:0] RegSel,
  input  [1:0] OutCSel,
  output [7:0] OutC
);

  wire [7:0] AR_q, PC_q, SP_q;

  Project1_8_bit_Register PC (.Clear(Clear), .Load(Load), .Clock(Clock), .FunSel(FunSel), .E(RegSel[2]), .Q(PC_q));
  Project1_8_bit_Register AR (.Clear(Clear), .Load(Load), .Clock(Clock), .FunSel(FunSel), .E(RegSel[1]), .Q(AR_q));
  Project1_8_bit_Register SP (.Clear(Clear), .Load(Load), .Clock(Clock), .FunSel(FunSel), .E(RegSel[0]), .Q(SP_q));
  Multiplexer #(.select(2), .width(8), .enable("false")) multiplexer_1 (
    .in0(PC_q), .in1(PC_q), .in2(AR_q), .in3(SP_q), .out(OutC), .sel(OutCSel));
endmodule

module Project2_ALU (
  input  [7:0] A,
  input  [7:0] B,
  input  clock,
  input  [3:0] FunSel,
  output [7:0] OutAlu,
  output [3:0] ZCNO
);

  wire A_B_2_cout, A_B_2_overflow, A_B_C_cout, A_B_C_overflow, A_B_cout, A_B_overflow, ASLA_overf,
       ASRA_overf, CSLA_cout, CSLA_overf, CSRA_cout, CSRA_overf, d_ff_1_q, LSLA_carryout, LSRA_carryout;
  wire [6:0] multiplexer_2_out;
  wire [7:0] A_B_2_z, A_B_a_b, A_B_C_a_b, and_1_out, ASLA_out, ASRA_out, CSLA_out, CSRA_out, LSLA_out,
       LSRA_out, not_1_out, not_2_out, or_1_out, xor_1_out;

  assign not_1_out = ~B;  // NOT_Gate not_1, 8 bits wide
  Project2_A_B A_B (.A(A), .B(B), .Cin(1'b0), .Cout(A_B_cout), .a_b(A_B_a_b), .Overflow(A_B_overflow));
  Project2_A_B A_B_C (.A(A), .B(B), .Cin(d_ff_1_q), .Cout(A_B_C_cout), .a_b(A_B_C_a_b), .Overflow(A_B_C_overflow));
  Project2_A_B_2 A_B_2 (.A(A), .B(B), .Cout(A_B_2_cout), .z(A_B_2_z), .Overflow(A_B_2_overflow));
  assign and_1_out = A & B;  // AND_Gate and_1, 8 bits wide
  assign or_1_out = A | B;  // OR_Gate or_1, 8 bits wide
  assign not_2_out = ~A;  // NOT_Gate not_2, 8 bits wide
  assign xor_1_out = A ^ B;  // XOR_Gate xor_1, 8 bits wide
  Project2_LSL LSLA (.A(A), .out(LSLA_out), .Carryout(LSLA_carryout));
  Project2_LSR LSRA (.A(A), .out(LSRA_out), .carryout(LSRA_carryout));
  Project2_ASL ASLA (.A(A), .out(ASLA_out), .overf(ASLA_overf));
  Project2_ASR ASRA (.A(A), .out(ASRA_out), .overf(ASRA_overf));
  Project2_CSL CSLA (.A(A), .Cin(d_ff_1_q), .out(CSLA_out), .overf(CSLA_overf), .COUT(CSLA_cout));
  Project2_CSR CSRA (.A(A), .C(d_ff_1_q), .out(CSRA_out), .overf(CSRA_overf), .COUT(CSRA_cout));
  Multiplexer #(.select(4), .width(8), .enable("false")) multiplexer_1 (
    .in0(A), .in1(A_B_a_b), .in2(A_B_C_a_b), .in3(A_B_2_z), .in4(and_1_out), .in5(or_1_out), .in6(not_2_out),
    .in7(xor_1_out), .in8(LSLA_out), .in9(LSRA_out), .in10(ASLA_out), .in11(ASRA_out), .in12(CSLA_out),
    .in13(CSRA_out), .in14(B), .in15(not_1_out), .out(OutAlu), .sel(FunSel));
  Multiplexer #(.select(4), .width(8), .enable("false")) multiplexer_2 (
    .in0(A), .in1(A_B_a_b), .in2(A_B_C_a_b), .in3(A_B_2_z), .in4(and_1_out), .in5(or_1_out), .in6(not_2_out),
    .in7(xor_1_out), .in8(LSLA_out), .in9(LSRA_out), .in10(ASLA_out), .in12(CSLA_out), .in13(CSRA_out),
    .in14(B), .in15(not_1_out), .out({ZCNO[1], multiplexer_2_out}), .sel(FunSel));  // open: in11
  nor nor_1 (ZCNO[3], OutAlu[0], OutAlu[1], OutAlu[2], OutAlu[3], OutAlu[4], OutAlu[5], OutAlu[6], OutAlu[7]);
  Multiplexer #(.select(4), .enable("false")) multiplexer_3 (
    .in1(A_B_overflow), .in2(A_B_C_overflow), .in3(A_B_2_overflow), .in10(ASLA_overf), .in11(ASRA_overf),
    .in12(CSLA_overf), .in13(CSRA_overf), .out(ZCNO[0]), .sel(FunSel));  // open: in0, in4, in5, in6, in7, in8, in9, in14, in15
  Multiplexer #(.select(4), .enable("false")) multiplexer_4 (
    .in1(A_B_cout), .in2(A_B_C_cout), .in3(A_B_2_cout), .in8(LSLA_carryout), .in9(LSRA_carryout),
    .in12(CSLA_cout), .in13(CSRA_cout), .out(ZCNO[2]), .sel(FunSel));  // open: in0, in4, in5, in6, in7, in10, in11, in14, in15
  D_Flip_Flop d_ff_1 (.clk(clock), .D(ZCNO[2]), .Q(d_ff_1_q));  // open: Qn, preset, en, reset
endmodule

module Project2_A_B (
  input  Cin,
  input  [7:0] A,
  input  [7:0] B,
  output [7:0] a_b,
  output Cout,
  output Overflow
);

  wire and_1_out, and_2_out, not_1_out, not_2_out, not_3_out;

  Adder adder_1 (.a(A), .b(B), .out(a_b), .cin(Cin), .cout(Cout));
  not not_1 (not_1_out, a_b[7]);
  not not_2 (not_2_out, A[7]);
  not not_3 (not_3_out, B[7]);
  and and_1 (and_1_out, not_1_out, A[7], B[7]);
  and and_2 (and_2_out, a_b[7], not_2_out, not_3_out);
  or or_1 (Overflow, and_1_out, and_2_out);
endmodule

module Project2_A_B_2 (
  input  [7:0] A,
  input  [7:0] B,
  output [7:0] z,
  output Cout,
  output Overflow
);

  wire and_1_out, and_2_out, not_2_out, not_3_out, not_4_out;
  wire [7:0] not_1_out;

  assign not_1_out = ~B;  // NOT_Gate not_1, 8 bits wide
  Adder adder_1 (.a(A), .b(not_1_out), .out(z), .cin(1'b1), .cout(Cout));
  not not_2 (not_2_out, z[7]);
  not not_3 (not_3_out, A[7]);
  not not_4 (not_4_out, not_1_out[7]);
  and and_1 (and_1_out, not_2_out, A[7], not_1_out[7]);
  and and_2 (and_2_out, z[7], not_3_out, not_4_out);
  or or_1 (Overflow, and_1_out, and_2_out);
endmodule

module Project2_LSL (
  input  [7:0] A,
  output [7:0] out,
  output Carryout
);


  assign Carryout = A[7];
  assign out = {A[6:0], 1'b0};
endmodule

module Project2_LSR (
  input  [7:0] A,
  output [7:0] out,
  output carryout
);


  assign carryout = A[0];
  assign out = {1'b0, A[7:1]};
endmodule

module Project2_CSL (
  input  Cin,
  input  [7:0] A,
  output [7:0] out,
  output overf,
  output COUT
);

  xor xor_1 (overf, A[6], A[7]);

  assign COUT = A[7];
  assign out = {A[6:0], Cin};
endmodule

module Project2_CSR (
  input  [7:0] A,
  input  C,
  output [7:0] out,
  output overf,
  output COUT
);

  xor xor_1 (overf, C, A[7]);

  assign COUT = A[0];
  assign out = {C, A[7:1]};
endmodule

module Project2_ASL (
  input  [7:0] A,
  output [7:0] out,
  output overf
);

  xor xor_1 (overf, A[6], A[7]);

  assign out = {A[6:0], 1'b0};
endmodule

module Project2_ASR (
  input  [7:0] A,
  output [7:0] out,
  output overf
);

  xor xor_1 (overf, A[7], A[7]);

  assign out = {{2{A[7]}}, A[6:1]};
endmodule

module Project2_part_2 (
  input  [7:0] Clear,
  input  [1:0] FunSel,
  input  [3:0] RegSel,
  input  [3:0] FunSel_2,
  input  [1:0] OutASel,
  input  [1:0] OutBSel,
  input  [1:0] in_7,
  input  [7:0] Clear_2,
  input  [1:0] in_9,
  input  Clock,
  input  Clear_3,
  input  [1:0] FunSel_3,
  input  [2:0] RegSel_2,
  input  [1:0] OutCSel,
  input  L_H,
  input  [15:0] Clear_4,
  input  load,
  input  [1:0] FunSel_4,
  input  Enable,
  output [3:0] ZCNO,
  output [7:0] IR_815
);

  wire not_1_out;
  wire [7:0] Adress_register_outc, ALU_outalu, controlled_buffer_1_out, IR_Register_ir_07, multiplexer_1_out,
       multiplexer_2_out, Register_File_outa, Register_File_outb, undriven;

  Multiplexer #(.select(2), .width(8), .enable("false")) multiplexer_1 (
    .in0(ALU_outalu), .in1(Adress_register_outc), .in2(undriven), .in3(IR_Register_ir_07),
    .out(multiplexer_1_out), .sel(in_7));
  Project1_part_2c IR_Register (
    .Load(undriven), .L_H(L_H), .Clear(Clear_4), .FunSel(FunSel_4), .Clock(Clock), .E(Enable),
    .IR_07(IR_Register_ir_07), .IR_815(IR_815));  // open: Q
  Project1_Part_2a Register_File (
    .Clear(Clear), .Load(multiplexer_1_out), .Clock(Clock), .FunSel(FunSel), .RegSel(RegSel),
    .OutASel(OutASel), .OutBSel(OutBSel), .OutA(Register_File_outa), .OutB(Register_File_outb));
  Multiplexer #(.select(2), .width(8), .enable("false")) multiplexer_2 (
    .in0(ALU_outalu), .in2(IR_Register_ir_07), .in3(undriven), .out(multiplexer_2_out), .sel(in_9));  // open: in1
  Project2_ALU ALU (
    .A(Register_File_outa), .B(Register_File_outb), .clock(Clock), .FunSel(FunSel_2), .OutAlu(ALU_outalu),
    .ZCNO(ZCNO));
  Project1_Part_2b Adress_register (
    .Clear(Clear_2), .Load(multiplexer_2_out), .Clock(Clock), .FunSel(FunSel_3), .RegSel(RegSel_2),
    .OutCSel(OutCSel), .OutC(Adress_register_outc));
  not not_1 (not_1_out, load);
  assign controlled_buffer_1_out = load ? ALU_outalu : 8'bz;  // Controlled_Buffer controlled_buffer_1
  RAM ram_1 (
    .addr(Adress_register_outc), .data(controlled_buffer_1_out), .sel(1'b1), .clk(Clock), .ld(not_1_out),
    .clr(Clear_3));
endmodule
